# Fritzing sketch Esquema Electrico HubUsbBotonesArduino (saved by Fritzing 0.9.3b)
breadboards: 1

parts:
  Componente1 = Arduino Nano (Rev3.0)
  S1 = Pushbutton [package="[THT]"]
  LED1 = LED - 5mm [color="Blue (525nm)" package="5 mm [THT]"]
  LED2 = LED - 5mm [color="Red (633nm)" package="5 mm [THT]"]
  R2 = Resistor [tolerance=±5% resistance=220 package="0805 [SMD]"]
  4_Relay_Module1 = OPENMolo 4 Relay breakout board
  R1 = Resistor [tolerance=±5% resistance=220 package="2010 [SMD]"]
  R3 = Resistor [tolerance=±5% resistance=220 package=THT]

nets:
  N1: Componente1.D2, S1.Pin_1, S1.Pin_2, R3.Pin_0
  N2: Componente1.D4, 4_Relay_Module1.E4
  N3: Componente1.D5, 4_Relay_Module1.E3
  N4: Componente1.D6, 4_Relay_Module1.E2
  N5: Componente1.D7, 4_Relay_Module1.E1
  GND: Componente1.GND, S1.Pin_3, S1.Pin_4, LED1.cathode, LED2.cathode, 4_Relay_Module1.GND
  N6: Componente1.A2, R2.Pin_0
  N7: Componente1.A1, R1.Pin_0
  3V3: Componente1.3V3, 4_Relay_Module1.VCC, R3.Pin_1
  N8: LED1.anode, R1.Pin_1
  N9: LED2.anode, R2.Pin_1

custom parts:
  OPENMolo 4 Relay breakout board: Módulo de 8 relés de 10A optoaislados pensado para desarrollos rápidos basadon en microcontroladores o microcomputadoras. Estos módulos son diseñados con especial cuidado tanto en sus capacidades aisladoras para preservar equipos de mayor valor asi como en las fijaciones para evitar problemas a la hora de armar un prototipo o de fijarlo en un tablero definitivo. Una importante característica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

// code stored in the sketch: Untitled.ino
//Pin para identificar que esta activado el USB2
const byte mPin_LedUSB1= 24;
//Pin para identificar que esta activado el USB2
const byte mPin_LedUSB2= 25;


// Guarda El Usb Activo actualemtne
// 1: USB1
// 2: USB2 
byte mNumUsbActivo = 1;  


// Variable que determina se el boton esta pulado
boolean mBotonPulsado = false;


// Pines De Rele
const byte mPin_Rele1= 11;
const byte mPin_Rele2= 10;
const byte mPin_Rele3= 9;
const byte mPin_Rele4= 8;
const byte mPin_Boton=32;



void setup() {
  // put your setup code here, to run once:


  // Coloca los pines de el led como emisor
  pinMode(mPin_LedUSB1, OUTPUT);
  pinMode(mPin_LedUSB1, OUTPUT);
//Pin para identificar que esta activado el USB2
const byte mPin_LedUSB1= 24;
//Pin para identificar que esta activado el USB2
const byte mPin_LedUSB2= 25;


// Guarda El Usb Activo actualemtne
// 1: USB1
// 2: USB2 
byte mNumUsbActivo = 1;  


// Variable que determina se el boton esta pulado
boolean mBotonPulsado = false;


// Pines De Rele
const byte mPin_Rele1= 11;
const byte mPin_Rele2= 10;
const byte mPin_Rele3= 9;
const byte mPin_Rele4= 8;
const byte mPin_Boton=32;



void setup() {
  // put your setup code here, to run once:


  // Coloca los pines de el led como emisor
  pinMode(mPin_LedUSB1, OUTPUT);
  pinMode(mPin_LedUSB1, OUTPUT);


  // Coloca Pin de Boton como Receptor
  pinMode(mPin_Boton, IMPUT);
  
  // Deja el pin de led 
  digitalWrite(mPin_LedUSB1, HIGH);


}


void loop() {
  // put your main code here, to run repeatedly:


  mBotonPulsado = digitalRead(mPin_Boton); // Lee si el boton esta precionado


  if(mBotonPulsado == HIGH){
    digitalWrite(mPin_LedUSB2, low);


  }


}


// Metodo Utilizado para determinar que USB Enciendo 
// Este USB recibe por parametro 1 o 2 
// si en un futoro agrego USB Agrego usb que acepta
void encenderUSB (int pNumUSB){


  if (pNumUSB == 1){
    
  }
}//Pin para identificar que esta activado el USB2
const byte mPin_LedUSB1= 24;
//Pin para identificar que esta activado el USB2
const byte mPin_LedUSB2= 25;


// Guarda El Usb Activo actualemtne
// 1: USB1
// 2: USB2 
byte mNumUsbActivo = 1;  


// Variable que determina se el boton esta pulado
boolean mBotonPulsado = false;


// Pines De Rele
const byte mPin_Rele1= 11;
const byte mPin_Rele2= 10;
const byte mPin_Rele3= 9;
const byte mPin_Rele4= 8;
const byte mPin_Boton=32;



void setup() {
  // put your setup code here, to run once:


  // Coloca los pines de el led como emisor
  pinMode(mPin_LedUSB1, OUTPUT);
  pinMode(mPin_LedUSB1, OUTPUT);


  // Coloca Pin de Boton como Receptor
  pinMode(mPin_Boton, IMPUT);
  
  // Deja el pin de led 
  digitalWrite(mPin_LedUSB1, HIGH);


}


void loop() {
  // put your main code here, to run repeatedly:


  mBotonPulsado = digitalRead(mPin_Boton); // Lee si el boton esta precionado


  if(mBotonPulsado == HIGH){
    digitalWrite(mPin_LedUSB2, low);


  }


}


// Metodo Utilizado para determinar que USB Enciendo 
// Este USB recibe por parametro 1 o 2 
// si en un futoro agrego USB Agrego usb que acepta
void encenderUSB (int pNumUSB){


  if (pNumUSB == 1){
//Pin para identificar que esta activado el USB2
const byte mPin_LedUSB1= 24;
//Pin para identificar que esta activado el USB2
const byte mPin_LedUSB2= 25;


// Guarda El Usb Activo actualemtne
// 1: USB1
// 2: USB2 
byte mNumUsbActivo = 1;  


// Variable que determina se el boton esta pulado
boolean mBotonPulsado = false;


// Pines De Rele
const byte mPin_Rele1= 11;
const byte mPin_Rele2= 10;
const byte mPin_Rele3= 9;
const byte mPin_Rele4= 8;
const byte mPin_Boton=32;



void setup() {
  // put your setup code here, to run once:


  // Coloca los pines de el led como emisor
  pinMode(mPin_LedUSB1, OUTPUT);
  pinMode(mPin_LedUSB1, OUTPUT);


  // Coloca Pin de Boton como Receptor
  pinMode(mPin_Boton, IMPUT);
  
  // Deja el pin de led 
  digitalWrite(mPin_LedUSB1, HIGH);


}


void loop() {
  // put your main code here, to run repeatedly:


  mBotonPulsado = digitalRead(mPin_Boton); // Lee si el boton esta precionado


  if(mBotonPulsado == HIGH){
    digitalWrite(mPin_LedUSB2, low);


  }


}


// Metodo Utilizado para determinar que USB Enciendo 
// Este USB recibe por parametro 1 o 2 
// si en un futoro agrego USB Agrego usb que acepta
void encenderUSB (int pNumUSB){


  if (pNumUSB == 1){
    
  }
}
    
  }
}

  // Coloca Pin de Boton como Receptor
  pinMode(mPin_Boton, IMPUT);
  
  // Deja el pin de led 
  digitalWrite(mPin_LedUSB1, HIGH);


}


void loop() {
  // put your main code here, to run repeatedly:


  mBotonPulsado = digitalRead(mPin_Boton); // Lee si el boton esta precionado


  if(mBotonPulsado == HIGH){
    digitalWrite(mPin_LedUSB2, low);


  }


}


// Metodo Utilizado para determinar que USB Enciendo 
// Este USB recibe por parametro 1 o 2 
// si en un futoro agrego USB Agrego usb que acepta
void encenderUSB (int pNumUSB){


  if (pNumUSB == 1){
    
  }
}
