# Fritzing sketch Esquema Electrico (saved by Fritzing 0.9.3b)
breadboards: 1

parts:
  Componente1 = Arduino Nano (Rev3.0)
  S1 = Pushbutton [package="[THT]"]
  LED1 = LED - 5mm [color="Blue (525nm)" package="5 mm [THT]"]
  LED2 = LED - 5mm [color="Red (633nm)" package="5 mm [THT]"]
  R2 = Resistor [tolerance=±5% resistance=220 package="0805 [SMD]"]
  4_Relay_Module1 = OPENMolo 4 Relay breakout board
  R1 = Resistor [tolerance=±5% resistance=220 package="2010 [SMD]"]

nets:
  N1: Componente1.D2, S1.Pin_1, S1.Pin_2
  GND: Componente1.GND, LED1.cathode, LED2.cathode, 4_Relay_Module1.GND
  N2: Componente1.A2, R2.Pin_0
  N3: Componente1.A1, R1.Pin_0
  3V3: Componente1.3V3, S1.Pin_3, S1.Pin_4, 4_Relay_Module1.VCC
  N4: LED1.anode, R1.Pin_1
  N5: LED2.anode, R2.Pin_1

custom parts:
  OPENMolo 4 Relay breakout board: Módulo de 8 relés de 10A optoaislados pensado para desarrollos rápidos basadon en microcontroladores o microcomputadoras. Estos módulos son diseñados con especial cuidado tanto en sus capacidades aisladoras para preservar equipos de mayor valor asi como en las fijaciones para evitar problemas a la hora de armar un prototipo o de fijarlo en un tablero definitivo. Una importante característica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
